# Fritzing sketch OpenerPcr (saved by Fritzing 0.8.0b)
breadboards: 6

parts:
  LCD = LCD screen
  Peltier = Peltier Element
  External_power_supply = Power plug [part_number="Power supply"]
  External_power_supply_connector1 = female pin header, 4 pins [form="♀ (female)"]
  H_bridge_Control = female pin header, 5 pins [form="♀ (female)"]
  Arduino1 = Arduino
  R_LCD = Rotary Potentiometer (Small) [maximum_resistance=100kΩ]
  Relay_board = female pin header, 4 pins [form="♀ (female)"]
  CT = female pin header, 2 pins [form="♀ (female)"]
  T = Temperature Sensor (Thermistor) [thermistor_type=NTC package=THT]
  R_T = Resistor [tolerance=±5% resistance=10k package=THT]
  C_Fan = female pin header, 3 pins [form="♀ (female)"]
  C_ExtPow = shrouded pin header, 24 pins [form="♂ (shrouded male)"]

nets:
  VSS: LCD.VSS, LCD.R/W, H_bridge_Control.pin5, Arduino1.GND, R_LCD.leg2, Relay_board.pin4, R_T.Pin_1, C_Fan.pin3
  VDD: LCD.VDD, Arduino1.+5V, R_LCD.leg1, Relay_board.pin1, CT.pin1, T.pin_0
  N1: LCD.V0, R_LCD.wiper
  N2: LCD.RS, Arduino1.D8
  N3: LCD.E, Arduino1.D9
  N4: LCD.DB4, Arduino1.D10
  N5: LCD.DB5, Arduino1.D11
  N6: LCD.DB6, Arduino1.D12
  N7: LCD.DB7, Arduino1.D13
  N8: Peltier.pin1, External_power_supply_connector1.pin3
  N9: Peltier.pin2, External_power_supply_connector1.pin4
  N10: External_power_supply.GND, External_power_supply_connector1.pin2
  N11: External_power_supply.VCC, External_power_supply_connector1.pin1
  N12: H_bridge_Control.pin1, Arduino1.D2, Relay_board.pin2
  N13: H_bridge_Control.pin2, Arduino1.D3, Relay_board.pin3
  N14: H_bridge_Control.pin3, Arduino1.D4
  N15: H_bridge_Control.pin4, Arduino1.D5
  N16: Arduino1.A0, CT.pin2, T.pin_1, R_T.Pin_0
  N17: Arduino1.A1, C_Fan.pin1
  N18: Arduino1.A5, C_Fan.pin2
  N19: C_ExtPow.pin1, C_ExtPow.pin24
  N20: C_ExtPow.pin2, C_ExtPow.pin23
  N21: C_ExtPow.pin3, C_ExtPow.pin22
  N22: C_ExtPow.pin4, C_ExtPow.pin21
  N23: C_ExtPow.pin5, C_ExtPow.pin20
  N24: C_ExtPow.pin6, C_ExtPow.pin19
  N25: C_ExtPow.pin7, C_ExtPow.pin18
  N26: C_ExtPow.pin8, C_ExtPow.pin17
  N27: C_ExtPow.pin9, C_ExtPow.pin16
  N28: C_ExtPow.pin10, C_ExtPow.pin15
  N29: C_ExtPow.pin11, C_ExtPow.pin14
  N30: C_ExtPow.pin12, C_ExtPow.pin13

notes:
  H bridge breakout board
  External power
  Thermistor board
  1: Termistor pin #1
  2: Termistor pin #2
  Our external power supply
  H bridge breakout board
  Control
  1: external power source A
  2: external power source B
  3: load pin A
  4: load pin B
  1. 1: IL1
  2. 2: IL2
  3. 3: IH1
  4. 4: IH2
  5. GND
  Power and ground
  1. 5 V
  2. 1: IL1
  3. 2: IL2
  4. GND
  Relay board
  OpenerPCR v.1.3
  DIY Bio Groningen
  by assert, 2014-02-01
  Version 1.3:
  - fixed error (again) in thermistor connection
  - removed thermistor from PCB: use the connectors for it
  Version 1.2:
  - fixed error in thermistor connection
  Version 1.1:
  - use an extra pin, to be able to turn the Peltier off
  - removed some unused connectors
  Fan control
  1: Set speed (0V = max, 5V = off)
  2. Read the speed (RPM counter)
  3. Ground
  Connector to power supply
